# Fritzing sketch Untitled Sketch (saved by Fritzing 0.9.10b)
breadboards: 1

parts:
  Pico_H1 = Raspberry Pi Pico H
  S1 = Pushbutton [package="[THT]"]
  LED1 = 7-SEGMENT-4DIGIT-YOUNGSUN [package=7-segment-4digit-youngsun-longpads]

nets:
  N1: Pico_H1.3V3, S1.Pin_1, S1.Pin_2
  N2: Pico_H1.GP12, LED1.DIG4
  N3: Pico_H1.GP11, LED1.DIG3
  N4: Pico_H1.GP10, LED1.DIG2
  N5: Pico_H1.GP9, LED1.DIG1
  N6: Pico_H1.GP8, LED1.DP
  N7: Pico_H1.GP7, LED1.G
  N8: Pico_H1.GP6, LED1.F
  N9: Pico_H1.GP5, LED1.E
  N10: Pico_H1.GP4, LED1.D
  N11: Pico_H1.GP3, LED1.C
  N12: Pico_H1.GP2, LED1.B
  N13: Pico_H1.GP1, LED1.A
  N14: Pico_H1.GP0, S1.Pin_3, S1.Pin_4

custom parts:
  Raspberry Pi Pico H: Raspberry Pi Pico H. Based around the RP2040 microcontroller the Pico H is a low cost microcontroller device bringing Raspberry Pi quality, cost, and easy of use to the microcontroller space.
