# Fritzing sketch pico_7_segment_clock (saved by Fritzing 0.9.10b)
circuit board: 17.9633cm x 7.7167cm
breadboards: 1

parts:
  S1 = Pushbutton [package="[THT]"]
  LED1 = 7-SEGMENT-4DIGIT-YOUNGSUN [package=7-segment-4digit-youngsun-longpads]
  Pico_H1 = Raspberry Pi Pico H

nets:
  N1: S1.Pin_1, S1.Pin_2, Pico_H1.3V3
  N2: S1.Pin_3, S1.Pin_4, Pico_H1.GP0
  N3: LED1.DIG1, Pico_H1.GP9
  N4: LED1.DIG2, Pico_H1.GP10
  N5: LED1.D, Pico_H1.GP4
  N6: LED1.E, Pico_H1.GP5
  N7: LED1.DIG3, Pico_H1.GP11
  N8: LED1.DP, Pico_H1.GP8
  N9: LED1.DIG4, Pico_H1.GP12
  N10: LED1.F, Pico_H1.GP6
  N11: LED1.C, Pico_H1.GP3
  N12: LED1.A, Pico_H1.GP1
  N13: LED1.G, Pico_H1.GP7
  N14: LED1.B, Pico_H1.GP2

custom parts:
  Raspberry Pi Pico H: Raspberry Pi Pico H. Based around the RP2040 microcontroller the Pico H is a low cost microcontroller device bringing Raspberry Pi quality, cost, and easy of use to the microcontroller space.
